# Fritzing sketch MachineSchematic (saved by Fritzing 0.8.7b)

parts:
  U2 = ESP32S-HiLetgo [part_number=ESP32S-HiLetgo]
  LED5 = LED - 5mm [color="Red (633nm)" package="5 mm [THT]"]
  LED6 = LED - 5mm [color="Red (633nm)" package="5 mm [THT]"]  # not connected
  LED7 = LED - 5mm [color="Red (633nm)" package="5 mm [THT]"]  # not connected
  LED8 = LED - 5mm [color="Red (633nm)" package="5 mm [THT]"]
  Bauteil2 = OLED Monochrome 128x32 I2C [part_number=931]
  S3 = SWITCH-MOMENTARY-2 [package=tactile-pth]  # not connected
  S4 = SWITCH-MOMENTARY-2 [package=tactile-pth]
  R7 = Resistor [tolerance=±5% resistance=220 package=THT]
  R8 = Resistor [tolerance=±5% resistance=220 package=THT]
  R9 = Resistor [tolerance=±5% resistance=220 package=THT]  # not connected
  R10 = Resistor [tolerance=±5% resistance=220 package=THT]
  R11 = Resistor [tolerance=±5% resistance=220 package=THT]
  R12 = Resistor [tolerance=±5% resistance=220 package=THT]

nets:
  N1: U2.3.3, Bauteil2.RESET
  N2: U2.GND, LED5.cathode, LED8.cathode, R10.Pin_1
  N3: U2.VIN, S4.1
  N4: U2.GPIO17, R7.Pin_1
  N5: U2.GPIO5, R8.Pin_1
  N6: U2.GPIO18, R11.Pin_1
  N7: U2.GPIO19, R12.Pin_1
  N8: U2.GPIO21, Bauteil2.SDA
  N9: U2.GPIO22, Bauteil2.SCL

notes:
  Abbrechen
  Ok

custom parts:
  ESP32S-HiLetgo: HiLetgo ESP-WROOM-32 ESP32 ESP-32S Development Board 2.4GHz Dual-Mode WiFi + Bluetooth Dual Cores Microcontroller The ESP32 integrated with Antenna switches, RF Balun, power amplifiers, low-noise amplifiers, filters, and management modules, and the entire solution occupies the least area of PCB. 2.4 GHz Wi-Fi plus Bluetooth dual-mode chip, with TSMC Ultra-low power consumption 40nm technology,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
  OLED Monochrome 128x32 I2C: These displays are small, only about 1" diagonal, but very readable due to the high contrast of an OLED display. This display is made of 128x32 individual white OLED pixels, each one is turned on or off by the controller chip. Because the display makes its own light, no backlight is required. This reduces the power required to run the OLED and is why the display has such high contrast; we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
